# Fritzing sketch 02 (saved by Fritzing 0.9.3b)
breadboards: 1

parts:
  J1 = Piezo Speaker
  부품1 = Arduino Uno (Rev3)
  R1 = Rotary Potentiometer (Small) [maximum_resistance=100kΩ package=THT]

nets:
  N1: J1.pin1, 부품1.GND, R1.leg1
  N2: J1.pin2, 부품1.D7
  N3: 부품1.A0, R1.wiper
  N4: 부품1.5V, R1.leg2
