# Fritzing sketch 03 (saved by Fritzing 0.9.3b)
breadboards: 1

parts:
  Ardunio_UNO = Arduino Uno (Rev3)
  R1 = Photocell (LDR) [package=THT]
  J1 = Piezo Speaker
  R2 = Resistor [tolerance=±5% resistance=10k package=THT]

nets (from the schematic view):
  N1: Ardunio_UNO.A0, R1.pin_0, R2.Pin_1
  N2: Ardunio_UNO.GND, J1.pin1
  N3: Ardunio_UNO.D7, J1.pin2
  N4: Ardunio_UNO.5V, R2.Pin_0
