# Fritzing sketch 04 (saved by Fritzing 0.9.3b)
breadboards: 1

parts:
  부품1 = Arduino Uno (Rev3)
  J1 = Piezo Speaker
  R1 = Resistor [tolerance=±5% resistance=10k package=THT]
  S1 = Pushbutton [package="[SMD]"]

nets:
  N1: 부품1.D8, R1.Pin_0, S1.Pin_3, S1.Pin_4
  N2: 부품1.AREF, J1.pin1, R1.Pin_1
  N3: 부품1.D7, J1.pin2
  N4: 부품1.5V, S1.Pin_1, S1.Pin_2
